// Logisim project second.circ as structural Verilog: 1 circuit, main circuit main
module main (
);

  wire and_1_out, and_2_out, and_3_out, and_4_out, Clock_out, d_ff_1_q, d_ff_1_qn, d_ff_2_q, d_ff_2_qn,
       d_ff_3_q, d_ff_3_qn, d_ff_4_q, din_0_out, din_1_out, din_2_out, din_3_out, Enable_out, Load_out,
       Mode_out, multiplexer_1_out, multiplexer_2_out, multiplexer_3_out, multiplexer_4_out,
       multiplexer_5_out, multiplexer_6_out, not_1_out, Reset_out, xor_1_out, xor_2_out, xor_3_out, xor_4_out;

  Clock Clock (.out(Clock_out));
  Button Reset (.out(Reset_out));
  Button Mode (.out(Mode_out));
  Button Load (.out(Load_out));
  Button Enable (.out(Enable_out));
  Button din_0 (.out(din_0_out));
  Multiplexer #(.enable("false")) multiplexer_1 (
    .in0(d_ff_1_qn), .in1(din_0_out), .out(multiplexer_1_out), .sel(Load_out));
  LED dout_0 (.in(d_ff_1_q));
  D_Flip_Flop d_ff_1 (
    .clk(Clock_out), .D(multiplexer_1_out), .Q(d_ff_1_q), .Qn(d_ff_1_qn), .en(Enable_out), .reset(Reset_out));  // open: preset
  xor xor_1 (xor_1_out, d_ff_2_q, d_ff_1_q);
  Button din_1 (.out(din_1_out));
  not not_1 (not_1_out, xor_2_out);
  xor xor_2 (xor_2_out, xor_1_out, Mode_out);
  Multiplexer #(.enable("false")) multiplexer_2 (
    .in0(not_1_out), .in1(din_1_out), .out(multiplexer_2_out), .sel(Load_out));
  D_Flip_Flop d_ff_2 (
    .clk(Clock_out), .D(multiplexer_2_out), .Q(d_ff_2_q), .Qn(d_ff_2_qn), .en(Enable_out), .reset(Reset_out));  // open: preset
  LED dout_1 (.in(d_ff_2_q));
  and and_1 (and_1_out, d_ff_1_q, d_ff_2_q);
  and and_2 (and_2_out, d_ff_2_qn, d_ff_1_qn);
  Multiplexer #(.enable("false")) multiplexer_3 (
    .in0(and_2_out), .in1(and_1_out), .out(multiplexer_3_out), .sel(Mode_out));
  Button din_2 (.out(din_2_out));
  xor xor_3 (xor_3_out, d_ff_3_q, multiplexer_3_out);
  Multiplexer #(.enable("false")) multiplexer_4 (
    .in0(xor_3_out), .in1(din_2_out), .out(multiplexer_4_out), .sel(Load_out));
  LED dout_2 (.in(d_ff_3_q));
  D_Flip_Flop d_ff_3 (
    .clk(Clock_out), .D(multiplexer_4_out), .Q(d_ff_3_q), .Qn(d_ff_3_qn), .en(Enable_out), .reset(Reset_out));  // open: preset
  and and_3 (and_3_out, and_1_out, d_ff_3_q);
  and and_4 (and_4_out, d_ff_3_qn, and_2_out);
  xor xor_4 (xor_4_out, d_ff_4_q, multiplexer_5_out);
  Multiplexer #(.enable("false")) multiplexer_5 (
    .in0(and_4_out), .in1(and_3_out), .out(multiplexer_5_out), .sel(Mode_out));
  Button din_3 (.out(din_3_out));
  Multiplexer #(.enable("false")) multiplexer_6 (
    .in0(xor_4_out), .in1(din_3_out), .out(multiplexer_6_out), .sel(Load_out));
  LED dout_3 (.in(d_ff_4_q));
  D_Flip_Flop d_ff_4 (
    .clk(Clock_out), .D(multiplexer_6_out), .Q(d_ff_4_q), .en(Enable_out), .reset(Reset_out));  // open: Qn, preset
endmodule
